# Fritzing sketch Prototype1 (saved by Fritzing 0.9.3b)
breadboards: 1

parts:
  Part1 = Arduino Uno (Rev3)
  U1 = LCD-16X2 [package=lcd-16x2]
  R1 = Resistor [tolerance=±5% resistance=220 package=THT]
  R2 = Resistor [tolerance=±5% resistance=4.7k package="1206 [SMD]"]
  DS1 = DS18B20 1-Wire Temperature Sensor [part_number=DS18B20]
  Humidity_sensor = IC, DIP package, 4 pins [chip_label=Humidity]
  U2 = ESP8266 WiFi Module [part_number=ESP8266]

nets:
  N1: Part1.A0, Humidity_sensor.pin1
  N2: Part1.D9_PWM, Part1.D11_PWM/MOSI, U1.E, U2.RXD
  N3: Part1.D10_PWM/SS, Part1.D13/SCK, R2.Pin_0, DS1.DQ, U2.TXD
  N4: Part1.D12/MISO, U1.RS
  N5: Part1.D2, U1.DB4
  N6: Part1.D3_PWM, U1.DB5
  N7: Part1.D4, U1.DB6
  N8: Part1.D5_PWM, U1.DB7
  3V3: Part1.3V3, U2.VCC, U2.CH_PD
  VDD: Part1.5V, U1.VDD, R1.Pin_0, R2.Pin_1, DS1.VDD, Humidity_sensor.pin4
  GND: Part1.GND, U1.VSS, U1.VO, U1.R_W, U1.K, DS1.GND, Humidity_sensor.pin3, U2.GND
  N9: U1.A, R1.Pin_1

custom parts:
  ESP8266 WiFi Module: Generic WiFi Module based on the ESP8266 with onboard PCB antenna and UART communications
